# Fritzing sketch ATmega128_breakout_setup (saved by Fritzing 0.9.2b)

parts:
  CP1 = Explore USB to UART [package="DIP (Dual Inline) [THT]"]
  D_\Github\ATMega-128-Break-Out-BoardDVB-12007\Others\Fritzing1 = Explore ATMEGA-128

nets:
  N1: CP1.pin1, D_\Github\ATMega-128-Break-Out-BoardDVB-12007\Others\Fritzing1.pin_57
  N2: CP1.pin3, D_\Github\ATMega-128-Break-Out-BoardDVB-12007\Others\Fritzing1.pin_59
  N3: CP1.pin4, D_\Github\ATMega-128-Break-Out-BoardDVB-12007\Others\Fritzing1.pin_60
  N4: CP1.pin5, D_\Github\ATMega-128-Break-Out-BoardDVB-12007\Others\Fritzing1.pin_61
  N5: CP1.pin7, D_\Github\ATMega-128-Break-Out-BoardDVB-12007\Others\Fritzing1.pin_63
