# Fritzing sketch ATmega128breakout_Switch and a LED (saved by Fritzing 0.9.2b)
breadboards: 2

parts:
  CP1 = Explore USB to UART [package="DIP (Dual Inline) [THT]"]
  R1 = Resistor [tolerance=±5% resistance=220 package=THT]
  LED1 = LED - 5mm [color="Red (633nm)" package="5 mm [THT]"]
  D_\Github\ATMega-128-Break-Out-BoardDVB-12007\Others\Fritzing1 = Explore ATMEGA-128
  S1 = Pushbutton [package="[THT]"]
  R2 = Resistor [tolerance=±5% resistance=220 package=THT]

nets:
  N1: CP1.pin1, D_\Github\ATMega-128-Break-Out-BoardDVB-12007\Others\Fritzing1.pin_57
  N2: CP1.pin2, D_\Github\ATMega-128-Break-Out-BoardDVB-12007\Others\Fritzing1.pin_58
  N3: CP1.pin3, D_\Github\ATMega-128-Break-Out-BoardDVB-12007\Others\Fritzing1.pin_59
  N4: CP1.pin4, D_\Github\ATMega-128-Break-Out-BoardDVB-12007\Others\Fritzing1.pin_60
  N5: CP1.pin5, D_\Github\ATMega-128-Break-Out-BoardDVB-12007\Others\Fritzing1.pin_61
  N6: CP1.pin6, D_\Github\ATMega-128-Break-Out-BoardDVB-12007\Others\Fritzing1.pin_62
  N7: CP1.pin7, D_\Github\ATMega-128-Break-Out-BoardDVB-12007\Others\Fritzing1.pin_63
  N8: R1.Pin_0, LED1.cathode
  N9: R1.Pin_1, D_\Github\ATMega-128-Break-Out-BoardDVB-12007\Others\Fritzing1.pin_39, S1.Pin_1, S1.Pin_2
  N10: LED1.anode, D_\Github\ATMega-128-Break-Out-BoardDVB-12007\Others\Fritzing1.PIN3
  N11: D_\Github\ATMega-128-Break-Out-BoardDVB-12007\Others\Fritzing1.pin_21, S1.Pin_3, S1.Pin_4, R2.Pin_0
  N12: D_\Github\ATMega-128-Break-Out-BoardDVB-12007\Others\Fritzing1.pin_40, R2.Pin_1
  N13: D_\Github\ATMega-128-Break-Out-BoardDVB-12007\Others\Fritzing1.pin_45, D_\Github\ATMega-128-Break-Out-BoardDVB-12007\Others\Fritzing1.pin_46, D_\Github\ATMega-128-Break-Out-BoardDVB-12007\Others\Fritzing1.pin_47, D_\Github\ATMega-128-Break-Out-BoardDVB-12007\Others\Fritzing1.pin_48
  N14: D_\Github\ATMega-128-Break-Out-BoardDVB-12007\Others\Fritzing1.pin_54, D_\Github\ATMega-128-Break-Out-BoardDVB-12007\Others\Fritzing1.pin_55, D_\Github\ATMega-128-Break-Out-BoardDVB-12007\Others\Fritzing1.pin_56
