# Fritzing sketch Interfacing RTC with Atmega128 Breakout (saved by Fritzing 0.9.2b)
breadboards: 2

parts:
  CP1 = Explore USB to UART [package="DIP (Dual Inline) [THT]"]
  D_\Github\ATMega-128-Break-Out-BoardDVB-12007\Others\Fritzing1 = Explore ATMEGA-128
  Breakout1 = LCD breakout [package="DIP (Dual Inline) [THT]"]
  LCD1 = LCD screen  # not connected
  C1 = EEPROM & RTC breakout

nets:
  N1: CP1.pin1, D_\Github\ATMega-128-Break-Out-BoardDVB-12007\Others\Fritzing1.pin_57
  N2: CP1.pin2, D_\Github\ATMega-128-Break-Out-BoardDVB-12007\Others\Fritzing1.pin_58
  N3: CP1.pin3, D_\Github\ATMega-128-Break-Out-BoardDVB-12007\Others\Fritzing1.pin_59
  N4: CP1.pin4, D_\Github\ATMega-128-Break-Out-BoardDVB-12007\Others\Fritzing1.pin_60
  N5: CP1.pin5, D_\Github\ATMega-128-Break-Out-BoardDVB-12007\Others\Fritzing1.pin_61
  N6: CP1.pin6, D_\Github\ATMega-128-Break-Out-BoardDVB-12007\Others\Fritzing1.pin_62
  N7: CP1.pin7, D_\Github\ATMega-128-Break-Out-BoardDVB-12007\Others\Fritzing1.pin_63
  N8: D_\Github\ATMega-128-Break-Out-BoardDVB-12007\Others\Fritzing1.PIN3, Breakout1.pin1
  N9: D_\Github\ATMega-128-Break-Out-BoardDVB-12007\Others\Fritzing1.pin_4, Breakout1.pin2
  N10: D_\Github\ATMega-128-Break-Out-BoardDVB-12007\Others\Fritzing1.pin_5, Breakout1.pin3
  N11: D_\Github\ATMega-128-Break-Out-BoardDVB-12007\Others\Fritzing1.pin_13, C1.SCL
  N12: D_\Github\ATMega-128-Break-Out-BoardDVB-12007\Others\Fritzing1.pin_14, C1.SDA
  N13: D_\Github\ATMega-128-Break-Out-BoardDVB-12007\Others\Fritzing1.pin_25, Breakout1.pin8
  N14: D_\Github\ATMega-128-Break-Out-BoardDVB-12007\Others\Fritzing1.pin_26, Breakout1.pin_9
  N15: D_\Github\ATMega-128-Break-Out-BoardDVB-12007\Others\Fritzing1.pin_27, Breakout1.pin_10
  N16: D_\Github\ATMega-128-Break-Out-BoardDVB-12007\Others\Fritzing1.pin_28, Breakout1.pin_11
  N17: D_\Github\ATMega-128-Break-Out-BoardDVB-12007\Others\Fritzing1.pin_39, Breakout1.pin_14, C1.GND
  N18: D_\Github\ATMega-128-Break-Out-BoardDVB-12007\Others\Fritzing1.pin_40, Breakout1.pin_15, C1.5V
  N19: D_\Github\ATMega-128-Break-Out-BoardDVB-12007\Others\Fritzing1.pin_45, D_\Github\ATMega-128-Break-Out-BoardDVB-12007\Others\Fritzing1.pin_46, D_\Github\ATMega-128-Break-Out-BoardDVB-12007\Others\Fritzing1.pin_47, D_\Github\ATMega-128-Break-Out-BoardDVB-12007\Others\Fritzing1.pin_48
  N20: D_\Github\ATMega-128-Break-Out-BoardDVB-12007\Others\Fritzing1.pin_54, D_\Github\ATMega-128-Break-Out-BoardDVB-12007\Others\Fritzing1.pin_55, D_\Github\ATMega-128-Break-Out-BoardDVB-12007\Others\Fritzing1.pin_56
