# Fritzing sketch Interfacing Seven Segment Display with Atmega128 Breakout (saved by Fritzing 0.9.2b)
breadboards: 2

parts:
  CP1 = Explore USB to UART [package="DIP (Dual Inline) [THT]"]
  D_\Github\ATMega-128-Break-Out-BoardDVB-12007\Others\Fritzing1 = Explore ATMEGA-128
  7_Segment1 = 7 Segment Display
  Q1 = NPN-Transistor [package="TO92 [THT]"]
  R1 = Resistor [tolerance=±5% resistance=220 package=THT]
  R2 = Resistor [tolerance=±5% resistance=220 package=THT]

nets:
  N1: CP1.pin1, D_\Github\ATMega-128-Break-Out-BoardDVB-12007\Others\Fritzing1.pin_57
  N2: CP1.pin2, D_\Github\ATMega-128-Break-Out-BoardDVB-12007\Others\Fritzing1.pin_58
  N3: CP1.pin3, D_\Github\ATMega-128-Break-Out-BoardDVB-12007\Others\Fritzing1.pin_59
  N4: CP1.pin4, D_\Github\ATMega-128-Break-Out-BoardDVB-12007\Others\Fritzing1.pin_60
  N5: CP1.pin5, D_\Github\ATMega-128-Break-Out-BoardDVB-12007\Others\Fritzing1.pin_61
  N6: CP1.pin6, D_\Github\ATMega-128-Break-Out-BoardDVB-12007\Others\Fritzing1.pin_62
  N7: CP1.pin7, D_\Github\ATMega-128-Break-Out-BoardDVB-12007\Others\Fritzing1.pin_63
  N8: D_\Github\ATMega-128-Break-Out-BoardDVB-12007\Others\Fritzing1.PIN3, 7_Segment1.Segment_A
  N9: D_\Github\ATMega-128-Break-Out-BoardDVB-12007\Others\Fritzing1.pin_4, 7_Segment1.Segment_B
  N10: D_\Github\ATMega-128-Break-Out-BoardDVB-12007\Others\Fritzing1.pin_5, 7_Segment1.Segment_C
  N11: D_\Github\ATMega-128-Break-Out-BoardDVB-12007\Others\Fritzing1.pin_6, 7_Segment1.Segment_D
  N12: D_\Github\ATMega-128-Break-Out-BoardDVB-12007\Others\Fritzing1.pin_7, 7_Segment1.Segment_E
  N13: D_\Github\ATMega-128-Break-Out-BoardDVB-12007\Others\Fritzing1.pin_8, 7_Segment1.Segment_F
  N14: D_\Github\ATMega-128-Break-Out-BoardDVB-12007\Others\Fritzing1.pin_9, 7_Segment1.Segment_G
  N15: D_\Github\ATMega-128-Break-Out-BoardDVB-12007\Others\Fritzing1.pin_10, 7_Segment1.Segment_DP
  N16: D_\Github\ATMega-128-Break-Out-BoardDVB-12007\Others\Fritzing1.pin_13, R2.Pin_0
  N17: D_\Github\ATMega-128-Break-Out-BoardDVB-12007\Others\Fritzing1.pin_40, R1.Pin_0
  N18: D_\Github\ATMega-128-Break-Out-BoardDVB-12007\Others\Fritzing1.pin_45, D_\Github\ATMega-128-Break-Out-BoardDVB-12007\Others\Fritzing1.pin_46, D_\Github\ATMega-128-Break-Out-BoardDVB-12007\Others\Fritzing1.pin_47, D_\Github\ATMega-128-Break-Out-BoardDVB-12007\Others\Fritzing1.pin_48
  N19: D_\Github\ATMega-128-Break-Out-BoardDVB-12007\Others\Fritzing1.pin_54, D_\Github\ATMega-128-Break-Out-BoardDVB-12007\Others\Fritzing1.pin_55, D_\Github\ATMega-128-Break-Out-BoardDVB-12007\Others\Fritzing1.pin_56
  N20: 7_Segment1.common_anode, Q1.C
  N21: Q1.E, R1.Pin_1
  N22: Q1.B, R2.Pin_1

custom parts:
  7 Segment Display: 7 Segment Display with common anode.
