# Fritzing sketch PIR basic interface (saved by Fritzing 0.9.2b)
breadboards: 1

parts:
  PIR1 = PIR sensor
  R1 = Resistor [tolerance=±5% resistance=220 package=THT]
  LED1 = LED - 5mm [color="Red (633nm)" package="5 mm [THT]"]
  BATT1 = 4xAA Switchable Battery Pack w/Bare Wire

nets:
  N1: PIR1.VDD, BATT1.POS
  N2: PIR1.SIG, R1.Pin_0
  N3: PIR1.GND, LED1.cathode, BATT1.NEG
  N4: R1.Pin_1, LED1.anode

custom parts:
  4xAA Switchable Battery Pack w/Bare Wire: 4xAA Switchable Battery Pack with Bare Wire connection
